// Logisim project minirv.circ as structural Verilog: 6 circuits, main circuit minirv
module minirv (
  input  reset
);

  wire clock_1_out, instruction_decoder_1_is_addi, instruction_decoder_1_is_jalr, or_1_out;
  wire [4:0] instruction_analyzer_1_rd, instruction_analyzer_1_rs1;
  wire [6:0] instruction_analyzer_1_opcode;
  wire [11:0] instruction_analyzer_1_imm;
  wire [31:0] adder_1_out, adder_2_out, bit_extender_1_out, fetcher_1_current_addr, fetcher_1_instruction,
       gpr_32x32bit_1_rdata1, multiplexer_1_out, multiplexer_2_out, multiplexer_3_out;

  Clock clock_1 (.out(clock_1_out));
  fetcher fetcher_1 (
    .jump_addr(multiplexer_1_out), .wenable(instruction_decoder_1_is_jalr), .clk(clock_1_out), .reset(reset),
    .current_addr(fetcher_1_current_addr), .instruction(fetcher_1_instruction));
  or or_1 (or_1_out, instruction_decoder_1_is_addi, instruction_decoder_1_is_jalr);
  Adder #(.width(32)) adder_1 (.a(fetcher_1_current_addr), .b(32'h4), .out(adder_1_out));  // open: cin, cout
  instruction_decoder instruction_decoder_1 (
    .instruction(fetcher_1_instruction), .is_addi(instruction_decoder_1_is_addi),
    .is_jalr(instruction_decoder_1_is_jalr));
  instruction_analyzer instruction_analyzer_1 (
    .instrction(fetcher_1_instruction), .opcode(instruction_analyzer_1_opcode),
    .rd(instruction_analyzer_1_rd), .rs1(instruction_analyzer_1_rs1), .imm(instruction_analyzer_1_imm));  // open: funct3
  GPR_32x32bit gpr_32x32bit_1 (
    .clk(clock_1_out), .wdata(multiplexer_3_out), .waddr(instruction_analyzer_1_rd), .wenable(or_1_out),
    .reset(reset), .raddr1(instruction_analyzer_1_rs1), .rdata1(gpr_32x32bit_1_rdata1));  // open: raddr2, rdata2
  assign bit_extender_1_out = {{20{instruction_analyzer_1_imm[11]}}, instruction_analyzer_1_imm};  // Bit_Extender bit_extender_1
  Adder #(.width(32)) adder_2 (
    .a(gpr_32x32bit_1_rdata1), .b(bit_extender_1_out), .out(adder_2_out));  // open: cin, cout
  Multiplexer #(.width(32)) multiplexer_1 (
    .in0({32{1'b0}}), .in1(adder_2_out), .out(multiplexer_1_out), .sel(instruction_decoder_1_is_jalr));
  Multiplexer #(.width(32)) multiplexer_2 (
    .in0({32{1'b0}}), .in1(adder_2_out), .out(multiplexer_2_out), .sel(instruction_decoder_1_is_addi));
  Multiplexer #(.width(32)) multiplexer_3 (
    .in0(multiplexer_2_out), .in1(adder_1_out), .out(multiplexer_3_out), .sel(instruction_decoder_1_is_jalr));

  // Notes on the sheet:
  //   imm+rs1
  //   jump_addr
  //   wdata
endmodule

module instruction_type_detector (
  input  [31:0] instruction,
  output is_i_load,
  output is_i_compute,
  output is_i,
  output is_i_jump
);

  Comparator #(.mode("unsigned"), .width(7)) comparator_1 (
    .a(7'b0000011), .b(instruction[6:0]), .eq(is_i_load));  // open: gt, lt
  Comparator #(.mode("unsigned"), .width(7)) comparator_2 (
    .a(7'b0010011), .b(instruction[6:0]), .eq(is_i_compute));  // open: gt, lt
  Comparator #(.mode("unsigned"), .width(7)) comparator_3 (
    .a(7'b1100111), .b(instruction[6:0]), .eq(is_i_jump));  // open: gt, lt
  or or_1 (is_i, is_i_load, is_i_compute, is_i_jump);
endmodule

module i_decoder (
  input  [31:0] instruction,
  output [6:0] opcode,
  output [4:0] rd,
  output [2:0] funct3,
  output [4:0] rs1,
  output [11:0] imm
);


  assign funct3 = instruction[14:12];
  assign imm = instruction[31:20];
  assign opcode = instruction[6:0];
  assign rd = instruction[11:7];
  assign rs1 = instruction[19:15];
endmodule

module instruction_analyzer (
  input  [31:0] instrction,
  output [6:0] opcode,
  output [4:0] rd,
  output [2:0] funct3,
  output [4:0] rs1,
  output [11:0] imm
);

  wire instruction_type_detector_1_is_i;
  wire [2:0] i_decoder_1_funct3;
  wire [4:0] i_decoder_1_rd, i_decoder_1_rs1;
  wire [6:0] i_decoder_1_opcode;
  wire [11:0] i_decoder_1_imm;

  instruction_type_detector instruction_type_detector_1 (
    .instruction(instrction), .is_i(instruction_type_detector_1_is_i));  // open: is_i_load, is_i_compute, is_i_jump
  i_decoder i_decoder_1 (
    .instruction(instrction), .opcode(i_decoder_1_opcode), .rd(i_decoder_1_rd), .funct3(i_decoder_1_funct3),
    .rs1(i_decoder_1_rs1), .imm(i_decoder_1_imm));
  Multiplexer #(.width(7)) multiplexer_1 (
    .in0({7{1'b0}}), .in1(i_decoder_1_opcode), .out(opcode), .sel(instruction_type_detector_1_is_i));
  Multiplexer #(.width(5)) multiplexer_2 (
    .in0({5{1'b0}}), .in1(i_decoder_1_rd), .out(rd), .sel(instruction_type_detector_1_is_i));
  Multiplexer #(.width(3)) multiplexer_3 (
    .in0(3'b000), .in1(i_decoder_1_funct3), .out(funct3), .sel(instruction_type_detector_1_is_i));
  Multiplexer #(.width(5)) multiplexer_4 (
    .in0({5{1'b0}}), .in1(i_decoder_1_rs1), .out(rs1), .sel(instruction_type_detector_1_is_i));
  Multiplexer #(.width(12)) multiplexer_5 (
    .in0({12{1'b0}}), .in1(i_decoder_1_imm), .out(imm), .sel(instruction_type_detector_1_is_i));
endmodule

module instruction_decoder (
  input  [31:0] instruction,
  output is_addi,
  output is_jalr
);

  wire comparator_1_eq, comparator_2_eq, instruction_type_detector_1_is_i_compute,
       instruction_type_detector_1_is_i_jump;
  wire [2:0] instruction_analyzer_1_funct3;

  instruction_analyzer instruction_analyzer_1 (
    .instrction(instruction), .funct3(instruction_analyzer_1_funct3));  // open: opcode, rd, rs1, imm
  Comparator #(.mode("unsigned"), .width(3)) comparator_1 (
    .a(instruction_analyzer_1_funct3), .b(3'b000), .eq(comparator_1_eq));  // open: gt, lt
  Comparator #(.mode("unsigned"), .width(3)) comparator_2 (
    .a(instruction_analyzer_1_funct3), .b(3'b000), .eq(comparator_2_eq));  // open: gt, lt
  instruction_type_detector instruction_type_detector_1 (
    .instruction(instruction), .is_i_compute(instruction_type_detector_1_is_i_compute),
    .is_i_jump(instruction_type_detector_1_is_i_jump));  // open: is_i_load, is_i
  and and_1 (is_addi, instruction_type_detector_1_is_i_compute, comparator_1_eq);
  and and_2 (is_jalr, instruction_type_detector_1_is_i_jump, comparator_2_eq);
endmodule

module fetcher (
  input  [31:0] jump_addr,
  input  wenable,
  input  clk,
  input  reset,
  output [31:0] current_addr,
  output [31:0] instruction
);

  wire [31:0] adder_1_out, multiplexer_1_out;

  Adder #(.width(32)) adder_1 (.a(current_addr), .b(32'h4), .out(adder_1_out));  // open: cin, cout
  Multiplexer #(.width(32)) multiplexer_1 (.in0(adder_1_out), .in1(jump_addr), .out(multiplexer_1_out), .sel(wenable));
  // ROM #(.line("quad")) rom_1: pin names not known; wires that end beside it: current_addr[7:0], instruction[7:0], instruction[15:8], instruction[23:16], instruction[31:24]
  Register #(.width(32)) PC (.D(multiplexer_1_out), .en(1'b1), .clk(clk), .Q(current_addr), .clr(reset));

  // Notes on the sheet:
  //   contents of rom_1 (hex, n*v repeats v):
  //   13 5 40 1 e7 0 0 1 e7 0 c0 0 67 0 c0 0 13 5 a5 0 67 80
endmodule
